// Logisim project ULA.circ as structural Verilog: 11 circuits, main circuit main
module main (
  input  [31:0] Entrada_A,
  input  [31:0] Entrada_B,
  input  [4:0] Seletor,
  output Zero,
  output [31:0] \Saída_S ,
  output Overflow
);

  ULA ula_1 (
    .Entrada_A(Entrada_A), .Overflow(Overflow), .Seletor(Seletor), .\Saída_S (\Saída_S ),
    .Entrada_B(Entrada_B), .Zero(Zero));

  // Notes on the sheet:
  //   00000=AND
  //   00001=OR
  //   00010=XOR
  //   00011=NAND
  //   00100=SOMA INT
  //   00101=SOMA NAT
  //   00110=SUBTRAIR
  //   01000=DESLOCAMENTO DIREITA
  //   01010=ROLL LEFT
  //   00111=DESLOCAMENTO ESQUERDA
  //   01001=DESLOCAMENTO DIREITA ARIT
endmodule

module ULA (
  input  [31:0] Entrada_A,
  input  [31:0] Entrada_B,
  input  [4:0] Seletor,
  output Overflow,
  output [31:0] \Saída_S ,
  output Zero
);

  wire and_2_out, and_3_out, and_4_out, and_5_out, celula_1_cout, celula_2_cout, celula_3_cout,
       celula_4_cout, celula_5_cout, celula_6_cout, celula_7_cout, celula_8_cout, celula_9_cout,
       celula_10_cout, celula_11_cout, celula_12_cout, celula_13_cout, celula_14_cout, celula_15_cout,
       celula_16_cout, celula_17_cout, celula_18_cout, celula_19_cout, celula_20_cout, celula_21_cout,
       celula_22_cout, celula_23_cout, celula_24_cout, celula_25_cout, celula_26_cout, celula_27_cout,
       celula_28_cout, celula_29_cout, celula_30_cout, celula_31_cout, celula_32_cout;
  wire [31:0] celula_31_s, not_1_out, \rollLeft_saída_a , \SLL_saída_a , \SRA_saída_a , \SRL_saída_a ;

  rollLeft rollLeft (.Entrada_A(Entrada_A), .Seletor(and_2_out), .\Saída_A (\rollLeft_saída_a ));
  SLL SLL (.Entrada_A(Entrada_A), .Seletor(and_3_out), .\Saída_A (\SLL_saída_a ));
  SRL SRL (.Entrada_A(Entrada_A), .in_2(and_4_out), .\Saída_A (\SRL_saída_a ));
  SRA SRA (.Entrada_A(Entrada_A), .in_2(and_5_out), .\Saída_A (\SRA_saída_a ));
  assign not_1_out = ~\Saída_S ;  // NOT_Gate not_1, 32 bits wide
  Multiplexer #(.select(5), .width(32), .enable("false")) multiplexer_1 (
    .in0(celula_31_s), .in1(celula_31_s), .in2(celula_31_s), .in3(celula_31_s), .in4(celula_31_s),
    .in5(celula_31_s), .in6(celula_31_s), .in7(\SLL_saída_a ), .in8(\SRL_saída_a ), .in9(\SRA_saída_a ),
    .in10(\rollLeft_saída_a ), .out(\Saída_S ), .sel(Seletor));  // open: in11, in12, in13, in14, in15, in16, in17, in18, in19, in20, in21, in22, in23, in24, in25, in26, in27, in28, in29, in30, in31
  and and_1 (Zero, not_1_out[0], not_1_out[1], not_1_out[2], not_1_out[3], not_1_out[4], not_1_out[5], not_1_out[6], not_1_out[7], not_1_out[8], not_1_out[9], not_1_out[10], not_1_out[11], not_1_out[12], not_1_out[13], not_1_out[14], not_1_out[15], not_1_out[16], not_1_out[17], not_1_out[18], not_1_out[19], not_1_out[20], not_1_out[21], not_1_out[22], not_1_out[23], not_1_out[24], not_1_out[25], not_1_out[26], not_1_out[27], not_1_out[28], not_1_out[29], not_1_out[30], not_1_out[31]);
  and and_2 (and_2_out, ~Seletor[0], Seletor[1], ~Seletor[2], Seletor[3], ~Seletor[4]);  // AND_Gate
  and and_3 (and_3_out, Seletor[0], Seletor[1], Seletor[2], ~Seletor[3], ~Seletor[4]);  // AND_Gate
  and and_4 (and_4_out, ~Seletor[0], ~Seletor[1], ~Seletor[2], Seletor[3], ~Seletor[4]);  // AND_Gate
  and and_5 (and_5_out, Seletor[0], ~Seletor[1], ~Seletor[2], Seletor[3], ~Seletor[4]);  // AND_Gate
  Celula celula_1 (
    .Cin(celula_2_cout), .Cout(celula_1_cout), .b(Entrada_B[30]), .a(Entrada_A[30]), .Seletor(Seletor),
    .S(celula_31_s[30]));
  Celula celula_2 (
    .Cin(celula_4_cout), .Cout(celula_2_cout), .b(Entrada_B[31]), .a(Entrada_A[31]), .Seletor(Seletor),
    .S(celula_31_s[31]));
  Celula celula_3 (
    .Cin(celula_1_cout), .Cout(celula_3_cout), .b(Entrada_B[28]), .a(Entrada_A[28]), .Seletor(Seletor),
    .S(celula_31_s[28]));
  Celula celula_4 (
    .Cin(celula_6_cout), .Cout(celula_4_cout), .b(Entrada_B[29]), .a(Entrada_A[29]), .Seletor(Seletor),
    .S(celula_31_s[29]));
  Celula celula_5 (
    .Cin(celula_3_cout), .Cout(celula_5_cout), .b(Entrada_B[26]), .a(Entrada_A[26]), .Seletor(Seletor),
    .S(celula_31_s[26]));
  Celula celula_6 (
    .Cin(celula_8_cout), .Cout(celula_6_cout), .b(Entrada_B[27]), .a(Entrada_A[27]), .Seletor(Seletor),
    .S(celula_31_s[27]));
  Celula celula_7 (
    .Cin(celula_5_cout), .Cout(celula_7_cout), .b(Entrada_B[24]), .a(Entrada_A[24]), .Seletor(Seletor),
    .S(celula_31_s[24]));
  Celula celula_8 (
    .Cin(celula_10_cout), .Cout(celula_8_cout), .b(Entrada_B[25]), .a(Entrada_A[25]), .Seletor(Seletor),
    .S(celula_31_s[25]));
  Celula celula_9 (
    .Cin(celula_7_cout), .Cout(celula_9_cout), .b(Entrada_B[23]), .a(Entrada_A[22]), .Seletor(Seletor),
    .S(celula_31_s[22]));
  Celula celula_10 (
    .Cin(celula_12_cout), .Cout(celula_10_cout), .b(Entrada_B[22]), .a(Entrada_A[23]), .Seletor(Seletor),
    .S(celula_31_s[23]));
  Celula celula_11 (
    .Cin(celula_9_cout), .Cout(celula_11_cout), .b(Entrada_B[21]), .a(Entrada_A[20]), .Seletor(Seletor),
    .S(celula_31_s[20]));
  Celula celula_12 (
    .Cin(celula_14_cout), .Cout(celula_12_cout), .b(Entrada_B[20]), .a(Entrada_A[21]), .Seletor(Seletor),
    .S(celula_31_s[21]));
  Celula celula_13 (
    .Cin(celula_11_cout), .Cout(celula_13_cout), .b(Entrada_B[19]), .a(Entrada_A[18]), .Seletor(Seletor),
    .S(celula_31_s[18]));
  Celula celula_14 (
    .Cin(celula_16_cout), .Cout(celula_14_cout), .b(Entrada_B[18]), .a(Entrada_A[19]), .Seletor(Seletor),
    .S(celula_31_s[19]));
  Celula celula_15 (
    .Cin(celula_13_cout), .Cout(celula_15_cout), .b(Entrada_B[17]), .a(Entrada_A[16]), .Seletor(Seletor),
    .S(celula_31_s[16]));
  Celula celula_16 (
    .Cin(celula_18_cout), .Cout(celula_16_cout), .b(Entrada_B[16]), .a(Entrada_A[17]), .Seletor(Seletor),
    .S(celula_31_s[17]));
  Celula celula_17 (
    .Cin(celula_15_cout), .Cout(celula_17_cout), .b(Entrada_B[15]), .a(Entrada_A[14]), .Seletor(Seletor),
    .S(celula_31_s[14]));
  Celula celula_18 (
    .Cin(celula_20_cout), .Cout(celula_18_cout), .b(Entrada_B[14]), .a(Entrada_A[15]), .Seletor(Seletor),
    .S(celula_31_s[15]));
  Celula celula_19 (
    .Cin(celula_17_cout), .Cout(celula_19_cout), .b(Entrada_B[13]), .a(Entrada_A[12]), .Seletor(Seletor),
    .S(celula_31_s[12]));
  Celula celula_20 (
    .Cin(celula_22_cout), .Cout(celula_20_cout), .b(Entrada_B[12]), .a(Entrada_A[13]), .Seletor(Seletor),
    .S(celula_31_s[13]));
  Celula celula_21 (
    .Cin(celula_19_cout), .Cout(celula_21_cout), .b(Entrada_B[11]), .a(Entrada_A[10]), .Seletor(Seletor),
    .S(celula_31_s[10]));
  Celula celula_22 (
    .Cin(celula_24_cout), .Cout(celula_22_cout), .b(Entrada_B[10]), .a(Entrada_A[11]), .Seletor(Seletor),
    .S(celula_31_s[11]));
  Celula celula_23 (
    .Cin(celula_21_cout), .Cout(celula_23_cout), .b(Entrada_B[9]), .a(Entrada_A[8]), .Seletor(Seletor),
    .S(celula_31_s[8]));
  Celula celula_24 (
    .Cin(celula_26_cout), .Cout(celula_24_cout), .b(Entrada_B[8]), .a(Entrada_A[9]), .Seletor(Seletor),
    .S(celula_31_s[9]));
  Celula celula_25 (
    .Cin(celula_23_cout), .Cout(celula_25_cout), .b(Entrada_B[7]), .a(Entrada_A[6]), .Seletor(Seletor),
    .S(celula_31_s[6]));
  Celula celula_26 (
    .Cin(celula_28_cout), .Cout(celula_26_cout), .b(Entrada_B[6]), .a(Entrada_A[7]), .Seletor(Seletor),
    .S(celula_31_s[7]));
  Celula celula_27 (
    .Cin(celula_25_cout), .Cout(celula_27_cout), .b(Entrada_B[5]), .a(Entrada_A[4]), .Seletor(Seletor),
    .S(celula_31_s[4]));
  Celula celula_28 (
    .Cin(celula_30_cout), .Cout(celula_28_cout), .b(Entrada_B[4]), .a(Entrada_A[5]), .Seletor(Seletor),
    .S(celula_31_s[5]));
  Celula celula_29 (
    .Cin(celula_27_cout), .Cout(celula_29_cout), .b(Entrada_B[3]), .a(Entrada_A[2]), .Seletor(Seletor),
    .S(celula_31_s[2]));
  Celula celula_30 (
    .Cin(celula_32_cout), .Cout(celula_30_cout), .b(Entrada_B[2]), .a(Entrada_A[3]), .Seletor(Seletor),
    .S(celula_31_s[3]));
  Celula celula_31 (
    .Cin(celula_29_cout), .Cout(celula_31_cout), .b(Entrada_B[1]), .a(Entrada_A[0]), .Seletor(Seletor),
    .S(celula_31_s[0]));
  Celula celula_32 (
    .Cin(1'b0), .Cout(celula_32_cout), .b(Entrada_B[0]), .a(Entrada_A[1]), .Seletor(Seletor),
    .S(celula_31_s[1]));
  OverFlowControler overflowcontroler_1 (
    .Overflow(Overflow), .Cin(celula_31_cout), .Seletor(Seletor), .a(Entrada_A[0]), .b(Entrada_B[1]),
    .s(celula_31_s[0]));

  // Notes on the sheet:
  //   Overflow
endmodule

module Celula (
  input  Cin,
  input  b,
  input  a,
  input  [4:0] Seletor,
  output S,
  output Cout
);

  wire and_1_out, and_2_out, nand_1_out, or_1_out, Somador_s, Somador_vai1, Subtrator_s, Subtrator_vai1,
       xor_1_out;

  and and_1 (and_1_out, a, b);
  or or_1 (or_1_out, a, b);
  xor xor_1 (xor_1_out, a, b);
  nand nand_1 (nand_1_out, a, b);
  Somador Somador (.a(a), .b(b), .Vem1(Cin), .Vai1(Somador_vai1), .S(Somador_s));
  Subtrator Subtrator (.a(a), .b(b), .Vem1(Cin), .Vai1(Subtrator_vai1), .S(Subtrator_s));
  Multiplexer #(.enable("false")) multiplexer_1 (.in0(Somador_vai1), .in1(Subtrator_vai1), .out(Cout), .sel(and_2_out));
  and and_2 (and_2_out, ~Seletor[0], Seletor[1], Seletor[2], ~Seletor[3], ~Seletor[4]);  // AND_Gate
  Multiplexer #(.select(5), .enable("false")) multiplexer_2 (
    .in0(and_1_out), .in1(or_1_out), .in2(xor_1_out), .in3(nand_1_out), .in4(Somador_s), .in5(Somador_s),
    .in6(Subtrator_s), .in7(a), .in8(a), .in9(a), .in10(a), .out(S), .sel(Seletor));  // open: in11, in12, in13, in14, in15, in16, in17, in18, in19, in20, in21, in22, in23, in24, in25, in26, in27, in28, in29, in30, in31
endmodule

module OverFlowControler (
  input  Cin,
  input  a,
  input  b,
  input  s,
  input  [4:0] Seletor,
  output Overflow
);

  wire and_1_out, and_2_out, and_3_out, or_1_out;

  Multiplexer #(.enable("false")) multiplexer_1 (.in0(Cin), .in1(or_1_out), .out(Overflow), .sel(and_1_out));
  and and_1 (and_1_out, Seletor[0], ~Seletor[1], Seletor[2], ~Seletor[3], ~Seletor[4]);  // AND_Gate
  or or_1 (or_1_out, and_2_out, and_3_out);
  and and_2 (and_2_out, a, b, ~s);  // AND_Gate
  and and_3 (and_3_out, ~a, ~b, s);  // AND_Gate

  // Notes on the sheet:
  //   00100 - Soma de Naturais
  //   00101 - Soma de Inteiros
endmodule

module Somador (
  input  Vem1,
  input  a,
  input  b,
  output S,
  output Vai1
);

  wire and_1_out, and_2_out, and_3_out, xor_1_out;

  and and_1 (and_1_out, b, a);
  and and_2 (and_2_out, b, Vem1);
  or or_1 (Vai1, and_1_out, and_2_out, and_3_out);
  and and_3 (and_3_out, a, Vem1);
  xor xor_1 (xor_1_out, a, b);
  xor xor_2 (S, Vem1, xor_1_out);
endmodule

module Subtrator (
  input  Vem1,
  input  a,
  input  b,
  output S,
  output Vai1
);

  wire and_1_out, and_2_out, and_3_out, xor_1_out;

  and and_1 (and_1_out, b, ~a);  // AND_Gate
  and and_2 (and_2_out, b, Vem1);
  or or_1 (Vai1, and_1_out, and_2_out, and_3_out);
  and and_3 (and_3_out, ~a, Vem1);  // AND_Gate
  xor xor_1 (xor_1_out, a, b);
  xor xor_2 (S, Vem1, xor_1_out);
endmodule

module SRL (
  input  [31:0] Entrada_A,
  input  in_2,
  output [31:0] \Saída_A 
);

  Multiplexer #(.enable("false")) multiplexer_1 (.in0(Entrada_A[31]), .in1(1'b0), .out(\Saída_A [31]), .sel(in_2));
  Multiplexer #(.enable("false")) multiplexer_2 (
    .in0(Entrada_A[30]), .in1(Entrada_A[31]), .out(\Saída_A [30]), .sel(in_2));
  Multiplexer #(.enable("false")) multiplexer_3 (
    .in0(Entrada_A[29]), .in1(Entrada_A[30]), .out(\Saída_A [29]), .sel(in_2));
  Multiplexer #(.enable("false")) multiplexer_4 (
    .in0(Entrada_A[28]), .in1(Entrada_A[29]), .out(\Saída_A [28]), .sel(in_2));
  Multiplexer #(.enable("false")) multiplexer_5 (
    .in0(Entrada_A[27]), .in1(Entrada_A[28]), .out(\Saída_A [27]), .sel(in_2));
  Multiplexer #(.enable("false")) multiplexer_6 (
    .in0(Entrada_A[26]), .in1(Entrada_A[27]), .out(\Saída_A [26]), .sel(in_2));
  Multiplexer #(.enable("false")) multiplexer_7 (
    .in0(Entrada_A[25]), .in1(Entrada_A[26]), .out(\Saída_A [25]), .sel(in_2));
  Multiplexer #(.enable("false")) multiplexer_8 (
    .in0(Entrada_A[24]), .in1(Entrada_A[25]), .out(\Saída_A [24]), .sel(in_2));
  Multiplexer #(.enable("false")) multiplexer_9 (
    .in0(Entrada_A[23]), .in1(Entrada_A[24]), .out(\Saída_A [23]), .sel(in_2));
  Multiplexer #(.enable("false")) multiplexer_10 (
    .in0(Entrada_A[22]), .in1(Entrada_A[23]), .out(\Saída_A [22]), .sel(in_2));
  Multiplexer #(.enable("false")) multiplexer_11 (
    .in0(Entrada_A[21]), .in1(Entrada_A[22]), .out(\Saída_A [21]), .sel(in_2));
  Multiplexer #(.enable("false")) multiplexer_12 (
    .in0(Entrada_A[20]), .in1(Entrada_A[21]), .out(\Saída_A [20]), .sel(in_2));
  Multiplexer #(.enable("false")) multiplexer_13 (
    .in0(Entrada_A[19]), .in1(Entrada_A[20]), .out(\Saída_A [19]), .sel(in_2));
  Multiplexer #(.enable("false")) multiplexer_14 (
    .in0(Entrada_A[18]), .in1(Entrada_A[19]), .out(\Saída_A [18]), .sel(in_2));
  Multiplexer #(.enable("false")) multiplexer_15 (
    .in0(Entrada_A[17]), .in1(Entrada_A[18]), .out(\Saída_A [17]), .sel(in_2));
  Multiplexer #(.enable("false")) multiplexer_16 (
    .in0(Entrada_A[16]), .in1(Entrada_A[17]), .out(\Saída_A [16]), .sel(in_2));
  Multiplexer #(.enable("false")) multiplexer_17 (
    .in0(Entrada_A[15]), .in1(Entrada_A[16]), .out(\Saída_A [15]), .sel(in_2));
  Multiplexer #(.enable("false")) multiplexer_18 (
    .in0(Entrada_A[14]), .in1(Entrada_A[15]), .out(\Saída_A [14]), .sel(in_2));
  Multiplexer #(.enable("false")) multiplexer_19 (
    .in0(Entrada_A[13]), .in1(Entrada_A[14]), .out(\Saída_A [13]), .sel(in_2));
  Multiplexer #(.enable("false")) multiplexer_20 (
    .in0(Entrada_A[12]), .in1(Entrada_A[13]), .out(\Saída_A [12]), .sel(in_2));
  Multiplexer #(.enable("false")) multiplexer_21 (
    .in0(Entrada_A[11]), .in1(Entrada_A[12]), .out(\Saída_A [11]), .sel(in_2));
  Multiplexer #(.enable("false")) multiplexer_22 (
    .in0(Entrada_A[10]), .in1(Entrada_A[11]), .out(\Saída_A [10]), .sel(in_2));
  Multiplexer #(.enable("false")) multiplexer_23 (
    .in0(Entrada_A[9]), .in1(Entrada_A[10]), .out(\Saída_A [9]), .sel(in_2));
  Multiplexer #(.enable("false")) multiplexer_24 (
    .in0(Entrada_A[8]), .in1(Entrada_A[9]), .out(\Saída_A [8]), .sel(in_2));
  Multiplexer #(.enable("false")) multiplexer_25 (
    .in0(Entrada_A[7]), .in1(Entrada_A[8]), .out(\Saída_A [7]), .sel(in_2));
  Multiplexer #(.enable("false")) multiplexer_26 (
    .in0(Entrada_A[6]), .in1(Entrada_A[7]), .out(\Saída_A [6]), .sel(in_2));
  Multiplexer #(.enable("false")) multiplexer_27 (
    .in0(Entrada_A[5]), .in1(Entrada_A[6]), .out(\Saída_A [5]), .sel(in_2));
  Multiplexer #(.enable("false")) multiplexer_28 (
    .in0(Entrada_A[4]), .in1(Entrada_A[5]), .out(\Saída_A [4]), .sel(in_2));
  Multiplexer #(.enable("false")) multiplexer_29 (
    .in0(Entrada_A[3]), .in1(Entrada_A[4]), .out(\Saída_A [3]), .sel(in_2));
  Multiplexer #(.enable("false")) multiplexer_30 (
    .in0(Entrada_A[2]), .in1(Entrada_A[3]), .out(\Saída_A [2]), .sel(in_2));
  Multiplexer #(.enable("false")) multiplexer_31 (
    .in0(Entrada_A[1]), .in1(Entrada_A[2]), .out(\Saída_A [1]), .sel(in_2));
  Multiplexer #(.enable("false")) multiplexer_32 (
    .in0(Entrada_A[0]), .in1(Entrada_A[1]), .out(\Saída_A [0]), .sel(in_2));
endmodule

module SLL (
  input  [31:0] Entrada_A,
  input  Seletor,
  output [31:0] \Saída_A 
);

  Multiplexer #(.enable("false")) multiplexer_1 (
    .in0(Entrada_A[31]), .in1(Entrada_A[30]), .out(\Saída_A [31]), .sel(Seletor));
  Multiplexer #(.enable("false")) multiplexer_2 (
    .in0(Entrada_A[30]), .in1(Entrada_A[29]), .out(\Saída_A [30]), .sel(Seletor));
  Multiplexer #(.enable("false")) multiplexer_3 (
    .in0(Entrada_A[29]), .in1(Entrada_A[28]), .out(\Saída_A [29]), .sel(Seletor));
  Multiplexer #(.enable("false")) multiplexer_4 (
    .in0(Entrada_A[28]), .in1(Entrada_A[27]), .out(\Saída_A [28]), .sel(Seletor));
  Multiplexer #(.enable("false")) multiplexer_5 (
    .in0(Entrada_A[27]), .in1(Entrada_A[26]), .out(\Saída_A [27]), .sel(Seletor));
  Multiplexer #(.enable("false")) multiplexer_6 (
    .in0(Entrada_A[26]), .in1(Entrada_A[25]), .out(\Saída_A [26]), .sel(Seletor));
  Multiplexer #(.enable("false")) multiplexer_7 (
    .in0(Entrada_A[25]), .in1(Entrada_A[24]), .out(\Saída_A [25]), .sel(Seletor));
  Multiplexer #(.enable("false")) multiplexer_8 (
    .in0(Entrada_A[24]), .in1(Entrada_A[23]), .out(\Saída_A [24]), .sel(Seletor));
  Multiplexer #(.enable("false")) multiplexer_9 (
    .in0(Entrada_A[23]), .in1(Entrada_A[22]), .out(\Saída_A [23]), .sel(Seletor));
  Multiplexer #(.enable("false")) multiplexer_10 (
    .in0(Entrada_A[22]), .in1(Entrada_A[21]), .out(\Saída_A [22]), .sel(Seletor));
  Multiplexer #(.enable("false")) multiplexer_11 (
    .in0(Entrada_A[21]), .in1(Entrada_A[20]), .out(\Saída_A [21]), .sel(Seletor));
  Multiplexer #(.enable("false")) multiplexer_12 (
    .in0(Entrada_A[20]), .in1(Entrada_A[19]), .out(\Saída_A [20]), .sel(Seletor));
  Multiplexer #(.enable("false")) multiplexer_13 (
    .in0(Entrada_A[19]), .in1(Entrada_A[18]), .out(\Saída_A [19]), .sel(Seletor));
  Multiplexer #(.enable("false")) multiplexer_14 (
    .in0(Entrada_A[18]), .in1(Entrada_A[17]), .out(\Saída_A [18]), .sel(Seletor));
  Multiplexer #(.enable("false")) multiplexer_15 (
    .in0(Entrada_A[17]), .in1(Entrada_A[16]), .out(\Saída_A [17]), .sel(Seletor));
  Multiplexer #(.enable("false")) multiplexer_16 (
    .in0(Entrada_A[16]), .in1(Entrada_A[15]), .out(\Saída_A [16]), .sel(Seletor));
  Multiplexer #(.enable("false")) multiplexer_17 (
    .in0(Entrada_A[15]), .in1(Entrada_A[14]), .out(\Saída_A [15]), .sel(Seletor));
  Multiplexer #(.enable("false")) multiplexer_18 (
    .in0(Entrada_A[14]), .in1(Entrada_A[13]), .out(\Saída_A [14]), .sel(Seletor));
  Multiplexer #(.enable("false")) multiplexer_19 (
    .in0(Entrada_A[13]), .in1(Entrada_A[12]), .out(\Saída_A [13]), .sel(Seletor));
  Multiplexer #(.enable("false")) multiplexer_20 (
    .in0(Entrada_A[12]), .in1(Entrada_A[11]), .out(\Saída_A [12]), .sel(Seletor));
  Multiplexer #(.enable("false")) multiplexer_21 (
    .in0(Entrada_A[11]), .in1(Entrada_A[10]), .out(\Saída_A [11]), .sel(Seletor));
  Multiplexer #(.enable("false")) multiplexer_22 (
    .in0(Entrada_A[10]), .in1(Entrada_A[9]), .out(\Saída_A [10]), .sel(Seletor));
  Multiplexer #(.enable("false")) multiplexer_23 (
    .in0(Entrada_A[9]), .in1(Entrada_A[8]), .out(\Saída_A [9]), .sel(Seletor));
  Multiplexer #(.enable("false")) multiplexer_24 (
    .in0(Entrada_A[8]), .in1(Entrada_A[7]), .out(\Saída_A [8]), .sel(Seletor));
  Multiplexer #(.enable("false")) multiplexer_25 (
    .in0(Entrada_A[7]), .in1(Entrada_A[6]), .out(\Saída_A [7]), .sel(Seletor));
  Multiplexer #(.enable("false")) multiplexer_26 (
    .in0(Entrada_A[6]), .in1(Entrada_A[5]), .out(\Saída_A [6]), .sel(Seletor));
  Multiplexer #(.enable("false")) multiplexer_27 (
    .in0(Entrada_A[5]), .in1(Entrada_A[4]), .out(\Saída_A [5]), .sel(Seletor));
  Multiplexer #(.enable("false")) multiplexer_28 (
    .in0(Entrada_A[4]), .in1(Entrada_A[3]), .out(\Saída_A [4]), .sel(Seletor));
  Multiplexer #(.enable("false")) multiplexer_29 (
    .in0(Entrada_A[3]), .in1(Entrada_A[2]), .out(\Saída_A [3]), .sel(Seletor));
  Multiplexer #(.enable("false")) multiplexer_30 (
    .in0(Entrada_A[2]), .in1(Entrada_A[1]), .out(\Saída_A [2]), .sel(Seletor));
  Multiplexer #(.enable("false")) multiplexer_31 (
    .in0(Entrada_A[1]), .in1(Entrada_A[0]), .out(\Saída_A [1]), .sel(Seletor));
  Multiplexer #(.enable("false")) multiplexer_32 (.in0(Entrada_A[0]), .in1(1'b0), .out(\Saída_A [0]), .sel(Seletor));
endmodule

module SRA (
  input  [31:0] Entrada_A,
  input  in_2,
  output [31:0] \Saída_A 
);

  Multiplexer #(.enable("false")) multiplexer_1 (
    .in0(Entrada_A[31]), .in1(Entrada_A[31]), .out(\Saída_A [31]), .sel(in_2));
  Multiplexer #(.enable("false")) multiplexer_2 (
    .in0(Entrada_A[30]), .in1(Entrada_A[31]), .out(\Saída_A [30]), .sel(in_2));
  Multiplexer #(.enable("false")) multiplexer_3 (
    .in0(Entrada_A[29]), .in1(Entrada_A[30]), .out(\Saída_A [29]), .sel(in_2));
  Multiplexer #(.enable("false")) multiplexer_4 (
    .in0(Entrada_A[28]), .in1(Entrada_A[29]), .out(\Saída_A [28]), .sel(in_2));
  Multiplexer #(.enable("false")) multiplexer_5 (
    .in0(Entrada_A[27]), .in1(Entrada_A[28]), .out(\Saída_A [27]), .sel(in_2));
  Multiplexer #(.enable("false")) multiplexer_6 (
    .in0(Entrada_A[26]), .in1(Entrada_A[27]), .out(\Saída_A [26]), .sel(in_2));
  Multiplexer #(.enable("false")) multiplexer_7 (
    .in0(Entrada_A[25]), .in1(Entrada_A[26]), .out(\Saída_A [25]), .sel(in_2));
  Multiplexer #(.enable("false")) multiplexer_8 (
    .in0(Entrada_A[24]), .in1(Entrada_A[25]), .out(\Saída_A [24]), .sel(in_2));
  Multiplexer #(.enable("false")) multiplexer_9 (
    .in0(Entrada_A[23]), .in1(Entrada_A[24]), .out(\Saída_A [23]), .sel(in_2));
  Multiplexer #(.enable("false")) multiplexer_10 (
    .in0(Entrada_A[22]), .in1(Entrada_A[23]), .out(\Saída_A [22]), .sel(in_2));
  Multiplexer #(.enable("false")) multiplexer_11 (
    .in0(Entrada_A[21]), .in1(Entrada_A[22]), .out(\Saída_A [21]), .sel(in_2));
  Multiplexer #(.enable("false")) multiplexer_12 (
    .in0(Entrada_A[20]), .in1(Entrada_A[21]), .out(\Saída_A [20]), .sel(in_2));
  Multiplexer #(.enable("false")) multiplexer_13 (
    .in0(Entrada_A[19]), .in1(Entrada_A[20]), .out(\Saída_A [19]), .sel(in_2));
  Multiplexer #(.enable("false")) multiplexer_14 (
    .in0(Entrada_A[18]), .in1(Entrada_A[19]), .out(\Saída_A [18]), .sel(in_2));
  Multiplexer #(.enable("false")) multiplexer_15 (
    .in0(Entrada_A[17]), .in1(Entrada_A[18]), .out(\Saída_A [17]), .sel(in_2));
  Multiplexer #(.enable("false")) multiplexer_16 (
    .in0(Entrada_A[16]), .in1(Entrada_A[17]), .out(\Saída_A [16]), .sel(in_2));
  Multiplexer #(.enable("false")) multiplexer_17 (
    .in0(Entrada_A[15]), .in1(Entrada_A[16]), .out(\Saída_A [15]), .sel(in_2));
  Multiplexer #(.enable("false")) multiplexer_18 (
    .in0(Entrada_A[14]), .in1(Entrada_A[15]), .out(\Saída_A [14]), .sel(in_2));
  Multiplexer #(.enable("false")) multiplexer_19 (
    .in0(Entrada_A[13]), .in1(Entrada_A[14]), .out(\Saída_A [13]), .sel(in_2));
  Multiplexer #(.enable("false")) multiplexer_20 (
    .in0(Entrada_A[12]), .in1(Entrada_A[13]), .out(\Saída_A [12]), .sel(in_2));
  Multiplexer #(.enable("false")) multiplexer_21 (
    .in0(Entrada_A[11]), .in1(Entrada_A[12]), .out(\Saída_A [11]), .sel(in_2));
  Multiplexer #(.enable("false")) multiplexer_22 (
    .in0(Entrada_A[10]), .in1(Entrada_A[11]), .out(\Saída_A [10]), .sel(in_2));
  Multiplexer #(.enable("false")) multiplexer_23 (
    .in0(Entrada_A[9]), .in1(Entrada_A[10]), .out(\Saída_A [9]), .sel(in_2));
  Multiplexer #(.enable("false")) multiplexer_24 (
    .in0(Entrada_A[8]), .in1(Entrada_A[9]), .out(\Saída_A [8]), .sel(in_2));
  Multiplexer #(.enable("false")) multiplexer_25 (
    .in0(Entrada_A[7]), .in1(Entrada_A[8]), .out(\Saída_A [7]), .sel(in_2));
  Multiplexer #(.enable("false")) multiplexer_26 (
    .in0(Entrada_A[6]), .in1(Entrada_A[7]), .out(\Saída_A [6]), .sel(in_2));
  Multiplexer #(.enable("false")) multiplexer_27 (
    .in0(Entrada_A[5]), .in1(Entrada_A[6]), .out(\Saída_A [5]), .sel(in_2));
  Multiplexer #(.enable("false")) multiplexer_28 (
    .in0(Entrada_A[4]), .in1(Entrada_A[5]), .out(\Saída_A [4]), .sel(in_2));
  Multiplexer #(.enable("false")) multiplexer_29 (
    .in0(Entrada_A[3]), .in1(Entrada_A[4]), .out(\Saída_A [3]), .sel(in_2));
  Multiplexer #(.enable("false")) multiplexer_30 (
    .in0(Entrada_A[2]), .in1(Entrada_A[3]), .out(\Saída_A [2]), .sel(in_2));
  Multiplexer #(.enable("false")) multiplexer_31 (
    .in0(Entrada_A[1]), .in1(Entrada_A[2]), .out(\Saída_A [1]), .sel(in_2));
  Multiplexer #(.enable("false")) multiplexer_32 (.in0(Entrada_A[0]), .in1(1'b0), .out(\Saída_A [0]), .sel(in_2));
endmodule

module rollLeft (
  input  [31:0] Entrada_A,
  input  Seletor,
  output [31:0] \Saída_A 
);

  Multiplexer #(.enable("false")) multiplexer_1 (
    .in0(Entrada_A[31]), .in1(Entrada_A[30]), .out(\Saída_A [31]), .sel(Seletor));
  Multiplexer #(.enable("false")) multiplexer_2 (
    .in0(Entrada_A[30]), .in1(Entrada_A[29]), .out(\Saída_A [30]), .sel(Seletor));
  Multiplexer #(.enable("false")) multiplexer_3 (
    .in0(Entrada_A[29]), .in1(Entrada_A[28]), .out(\Saída_A [29]), .sel(Seletor));
  Multiplexer #(.enable("false")) multiplexer_4 (
    .in0(Entrada_A[28]), .in1(Entrada_A[27]), .out(\Saída_A [28]), .sel(Seletor));
  Multiplexer #(.enable("false")) multiplexer_5 (
    .in0(Entrada_A[27]), .in1(Entrada_A[26]), .out(\Saída_A [27]), .sel(Seletor));
  Multiplexer #(.enable("false")) multiplexer_6 (
    .in0(Entrada_A[26]), .in1(Entrada_A[25]), .out(\Saída_A [26]), .sel(Seletor));
  Multiplexer #(.enable("false")) multiplexer_7 (
    .in0(Entrada_A[25]), .in1(Entrada_A[24]), .out(\Saída_A [25]), .sel(Seletor));
  Multiplexer #(.enable("false")) multiplexer_8 (
    .in0(Entrada_A[24]), .in1(Entrada_A[23]), .out(\Saída_A [24]), .sel(Seletor));
  Multiplexer #(.enable("false")) multiplexer_9 (
    .in0(Entrada_A[23]), .in1(Entrada_A[22]), .out(\Saída_A [23]), .sel(Seletor));
  Multiplexer #(.enable("false")) multiplexer_10 (
    .in0(Entrada_A[22]), .in1(Entrada_A[21]), .out(\Saída_A [22]), .sel(Seletor));
  Multiplexer #(.enable("false")) multiplexer_11 (
    .in0(Entrada_A[21]), .in1(Entrada_A[20]), .out(\Saída_A [21]), .sel(Seletor));
  Multiplexer #(.enable("false")) multiplexer_12 (
    .in0(Entrada_A[20]), .in1(Entrada_A[19]), .out(\Saída_A [20]), .sel(Seletor));
  Multiplexer #(.enable("false")) multiplexer_13 (
    .in0(Entrada_A[19]), .in1(Entrada_A[18]), .out(\Saída_A [19]), .sel(Seletor));
  Multiplexer #(.enable("false")) multiplexer_14 (
    .in0(Entrada_A[18]), .in1(Entrada_A[17]), .out(\Saída_A [18]), .sel(Seletor));
  Multiplexer #(.enable("false")) multiplexer_15 (
    .in0(Entrada_A[17]), .in1(Entrada_A[16]), .out(\Saída_A [17]), .sel(Seletor));
  Multiplexer #(.enable("false")) multiplexer_16 (
    .in0(Entrada_A[16]), .in1(Entrada_A[15]), .out(\Saída_A [16]), .sel(Seletor));
  Multiplexer #(.enable("false")) multiplexer_17 (
    .in0(Entrada_A[15]), .in1(Entrada_A[14]), .out(\Saída_A [15]), .sel(Seletor));
  Multiplexer #(.enable("false")) multiplexer_18 (
    .in0(Entrada_A[14]), .in1(Entrada_A[13]), .out(\Saída_A [14]), .sel(Seletor));
  Multiplexer #(.enable("false")) multiplexer_19 (
    .in0(Entrada_A[13]), .in1(Entrada_A[12]), .out(\Saída_A [13]), .sel(Seletor));
  Multiplexer #(.enable("false")) multiplexer_20 (
    .in0(Entrada_A[12]), .in1(Entrada_A[11]), .out(\Saída_A [12]), .sel(Seletor));
  Multiplexer #(.enable("false")) multiplexer_21 (
    .in0(Entrada_A[11]), .in1(Entrada_A[10]), .out(\Saída_A [11]), .sel(Seletor));
  Multiplexer #(.enable("false")) multiplexer_22 (
    .in0(Entrada_A[10]), .in1(Entrada_A[9]), .out(\Saída_A [10]), .sel(Seletor));
  Multiplexer #(.enable("false")) multiplexer_23 (
    .in0(Entrada_A[9]), .in1(Entrada_A[8]), .out(\Saída_A [9]), .sel(Seletor));
  Multiplexer #(.enable("false")) multiplexer_24 (
    .in0(Entrada_A[8]), .in1(Entrada_A[7]), .out(\Saída_A [8]), .sel(Seletor));
  Multiplexer #(.enable("false")) multiplexer_25 (
    .in0(Entrada_A[7]), .in1(Entrada_A[6]), .out(\Saída_A [7]), .sel(Seletor));
  Multiplexer #(.enable("false")) multiplexer_26 (
    .in0(Entrada_A[6]), .in1(Entrada_A[5]), .out(\Saída_A [6]), .sel(Seletor));
  Multiplexer #(.enable("false")) multiplexer_27 (
    .in0(Entrada_A[5]), .in1(Entrada_A[4]), .out(\Saída_A [5]), .sel(Seletor));
  Multiplexer #(.enable("false")) multiplexer_28 (
    .in0(Entrada_A[4]), .in1(Entrada_A[3]), .out(\Saída_A [4]), .sel(Seletor));
  Multiplexer #(.enable("false")) multiplexer_29 (
    .in0(Entrada_A[3]), .in1(Entrada_A[2]), .out(\Saída_A [3]), .sel(Seletor));
  Multiplexer #(.enable("false")) multiplexer_30 (
    .in0(Entrada_A[2]), .in1(Entrada_A[1]), .out(\Saída_A [2]), .sel(Seletor));
  Multiplexer #(.enable("false")) multiplexer_31 (
    .in0(Entrada_A[1]), .in1(Entrada_A[0]), .out(\Saída_A [1]), .sel(Seletor));
  Multiplexer #(.enable("false")) multiplexer_32 (
    .in0(Entrada_A[0]), .in1(Entrada_A[31]), .out(\Saída_A [0]), .sel(Seletor));
endmodule

module BarrelShifterR (
  input  [31:0] Entrada_A
);

  wire multiplexer_1_out, multiplexer_2_out, multiplexer_3_out, multiplexer_4_out, multiplexer_5_out,
       multiplexer_7_out, multiplexer_8_out, multiplexer_9_out, multiplexer_11_out, multiplexer_12_out,
       multiplexer_13_out, multiplexer_14_out, multiplexer_16_out, multiplexer_17_out, multiplexer_18_out,
       multiplexer_19_out, multiplexer_21_out, multiplexer_22_out, multiplexer_23_out, multiplexer_24_out,
       multiplexer_26_out, multiplexer_27_out, multiplexer_28_out, multiplexer_29_out, multiplexer_30_out,
       multiplexer_31_out, multiplexer_33_out, multiplexer_34_out, multiplexer_36_out, multiplexer_37_out,
       multiplexer_38_out, multiplexer_39_out, multiplexer_41_out, multiplexer_42_out, multiplexer_44_out,
       multiplexer_46_out, multiplexer_47_out, multiplexer_48_out, multiplexer_49_out, multiplexer_51_out,
       multiplexer_52_out, multiplexer_53_out, multiplexer_54_out, multiplexer_56_out, multiplexer_57_out,
       multiplexer_58_out, multiplexer_59_out, multiplexer_60_out, multiplexer_61_out, multiplexer_62_out,
       multiplexer_64_out, multiplexer_65_out, multiplexer_66_out, multiplexer_68_out, multiplexer_69_out,
       multiplexer_71_out, multiplexer_72_out, multiplexer_73_out, multiplexer_74_out, multiplexer_76_out,
       multiplexer_77_out, multiplexer_78_out, multiplexer_79_out, multiplexer_81_out, multiplexer_82_out,
       multiplexer_83_out, multiplexer_84_out, multiplexer_86_out, multiplexer_87_out, multiplexer_88_out,
       multiplexer_89_out, multiplexer_91_out, multiplexer_92_out, multiplexer_93_out, multiplexer_94_out,
       multiplexer_95_out, multiplexer_97_out, multiplexer_98_out, multiplexer_99_out, multiplexer_100_out,
       multiplexer_102_out, multiplexer_103_out, multiplexer_104_out, multiplexer_106_out,
       multiplexer_107_out, multiplexer_108_out, multiplexer_109_out, multiplexer_111_out,
       multiplexer_112_out, multiplexer_113_out, multiplexer_114_out, multiplexer_116_out,
       multiplexer_117_out, multiplexer_118_out, multiplexer_119_out, multiplexer_120_out,
       multiplexer_121_out, multiplexer_122_out, multiplexer_123_out, multiplexer_125_out,
       multiplexer_126_out, multiplexer_127_out, multiplexer_129_out, multiplexer_130_out,
       multiplexer_132_out, multiplexer_133_out, multiplexer_134_out, multiplexer_136_out,
       multiplexer_137_out, multiplexer_138_out, multiplexer_139_out, multiplexer_141_out,
       multiplexer_142_out, multiplexer_143_out, multiplexer_144_out, multiplexer_146_out,
       multiplexer_147_out, multiplexer_148_out, multiplexer_149_out, multiplexer_151_out,
       multiplexer_152_out, multiplexer_153_out, multiplexer_154_out, multiplexer_155_out,
       multiplexer_156_out, multiplexer_158_out, multiplexer_159_out, undriven;

  Multiplexer #(.enable("false")) multiplexer_1 (
    .in0(Entrada_A[0]), .in1(1'b0), .out(multiplexer_1_out), .sel(undriven));
  Multiplexer #(.enable("false")) multiplexer_2 (
    .in0(multiplexer_1_out), .in1(1'b0), .out(multiplexer_2_out), .sel(undriven));
  Multiplexer #(.enable("false")) multiplexer_3 (
    .in0(Entrada_A[1]), .in1(Entrada_A[0]), .out(multiplexer_3_out), .sel(undriven));
  Multiplexer #(.enable("false")) multiplexer_4 (
    .in0(multiplexer_2_out), .in1(1'b0), .out(multiplexer_4_out), .sel(undriven));
  Multiplexer #(.enable("false")) multiplexer_5 (
    .in0(multiplexer_4_out), .in1(1'b0), .out(multiplexer_5_out), .sel(undriven));
  Multiplexer #(.enable("false")) multiplexer_6 (.in0(multiplexer_5_out), .in1(1'b0), .sel(undriven));  // open: out
  Multiplexer #(.enable("false")) multiplexer_7 (
    .in0(multiplexer_3_out), .in1(1'b0), .out(multiplexer_7_out), .sel(undriven));
  Multiplexer #(.enable("false")) multiplexer_8 (
    .in0(multiplexer_7_out), .in1(1'b0), .out(multiplexer_8_out), .sel(undriven));
  Multiplexer #(.enable("false")) multiplexer_9 (
    .in0(multiplexer_8_out), .in1(1'b0), .out(multiplexer_9_out), .sel(undriven));
  Multiplexer #(.enable("false")) multiplexer_10 (.in0(multiplexer_9_out), .in1(1'b0), .sel(undriven));  // open: out
  Multiplexer #(.enable("false")) multiplexer_11 (
    .in0(Entrada_A[2]), .in1(Entrada_A[1]), .out(multiplexer_11_out), .sel(undriven));
  Multiplexer #(.enable("false")) multiplexer_12 (
    .in0(multiplexer_11_out), .in1(multiplexer_1_out), .out(multiplexer_12_out), .sel(undriven));
  Multiplexer #(.enable("false")) multiplexer_13 (
    .in0(multiplexer_12_out), .in1(1'b0), .out(multiplexer_13_out), .sel(undriven));
  Multiplexer #(.enable("false")) multiplexer_14 (
    .in0(multiplexer_13_out), .in1(1'b0), .out(multiplexer_14_out), .sel(undriven));
  Multiplexer #(.enable("false")) multiplexer_15 (.in0(multiplexer_14_out), .in1(1'b0), .sel(undriven));  // open: out
  Multiplexer #(.enable("false")) multiplexer_16 (
    .in0(Entrada_A[3]), .in1(Entrada_A[2]), .out(multiplexer_16_out), .sel(undriven));
  Multiplexer #(.enable("false")) multiplexer_17 (
    .in0(multiplexer_16_out), .in1(multiplexer_3_out), .out(multiplexer_17_out), .sel(undriven));
  Multiplexer #(.enable("false")) multiplexer_18 (
    .in0(multiplexer_17_out), .in1(1'b0), .out(multiplexer_18_out), .sel(undriven));
  Multiplexer #(.enable("false")) multiplexer_19 (
    .in0(multiplexer_18_out), .in1(1'b0), .out(multiplexer_19_out), .sel(undriven));
  Multiplexer #(.enable("false")) multiplexer_20 (.in0(multiplexer_19_out), .in1(1'b0), .sel(undriven));  // open: out
  Multiplexer #(.enable("false")) multiplexer_21 (
    .in0(Entrada_A[4]), .in1(Entrada_A[3]), .out(multiplexer_21_out), .sel(undriven));
  Multiplexer #(.enable("false")) multiplexer_22 (
    .in0(multiplexer_21_out), .in1(multiplexer_11_out), .out(multiplexer_22_out), .sel(undriven));
  Multiplexer #(.enable("false")) multiplexer_23 (
    .in0(multiplexer_22_out), .in1(multiplexer_2_out), .out(multiplexer_23_out), .sel(undriven));
  Multiplexer #(.enable("false")) multiplexer_24 (
    .in0(multiplexer_23_out), .in1(1'b0), .out(multiplexer_24_out), .sel(undriven));
  Multiplexer #(.enable("false")) multiplexer_25 (.in0(multiplexer_24_out), .in1(1'b0), .sel(undriven));  // open: out
  Multiplexer #(.enable("false")) multiplexer_26 (
    .in0(Entrada_A[5]), .in1(Entrada_A[4]), .out(multiplexer_26_out), .sel(undriven));
  Multiplexer #(.enable("false")) multiplexer_27 (
    .in0(multiplexer_26_out), .in1(multiplexer_16_out), .out(multiplexer_27_out), .sel(undriven));
  Multiplexer #(.enable("false")) multiplexer_28 (
    .in0(multiplexer_27_out), .in1(multiplexer_7_out), .out(multiplexer_28_out), .sel(undriven));
  Multiplexer #(.enable("false")) multiplexer_29 (
    .in0(multiplexer_28_out), .in1(1'b0), .out(multiplexer_29_out), .sel(undriven));
  Multiplexer #(.enable("false")) multiplexer_30 (
    .in0(Entrada_A[6]), .in1(Entrada_A[5]), .out(multiplexer_30_out), .sel(undriven));
  Multiplexer #(.enable("false")) multiplexer_31 (
    .in0(multiplexer_30_out), .in1(multiplexer_21_out), .out(multiplexer_31_out), .sel(undriven));
  Multiplexer #(.enable("false")) multiplexer_32 (.in0(multiplexer_29_out), .in1(1'b0), .sel(undriven));  // open: out
  Multiplexer #(.enable("false")) multiplexer_33 (
    .in0(multiplexer_31_out), .in1(multiplexer_12_out), .out(multiplexer_33_out), .sel(undriven));
  Multiplexer #(.enable("false")) multiplexer_34 (
    .in0(multiplexer_33_out), .in1(1'b0), .out(multiplexer_34_out), .sel(undriven));
  Multiplexer #(.enable("false")) multiplexer_35 (.in0(multiplexer_34_out), .in1(1'b0), .sel(undriven));  // open: out
  Multiplexer #(.enable("false")) multiplexer_36 (
    .in0(Entrada_A[7]), .in1(Entrada_A[6]), .out(multiplexer_36_out), .sel(undriven));
  Multiplexer #(.enable("false")) multiplexer_37 (
    .in0(multiplexer_36_out), .in1(multiplexer_26_out), .out(multiplexer_37_out), .sel(undriven));
  Multiplexer #(.enable("false")) multiplexer_38 (
    .in0(multiplexer_37_out), .in1(multiplexer_17_out), .out(multiplexer_38_out), .sel(undriven));
  Multiplexer #(.enable("false")) multiplexer_39 (
    .in0(multiplexer_38_out), .in1(1'b0), .out(multiplexer_39_out), .sel(undriven));
  Multiplexer #(.enable("false")) multiplexer_40 (.in0(multiplexer_39_out), .in1(1'b0), .sel(undriven));  // open: out
  Multiplexer #(.enable("false")) multiplexer_41 (
    .in0(Entrada_A[8]), .in1(Entrada_A[7]), .out(multiplexer_41_out), .sel(undriven));
  Multiplexer #(.enable("false")) multiplexer_42 (
    .in0(multiplexer_41_out), .in1(multiplexer_30_out), .out(multiplexer_42_out), .sel(undriven));
  Multiplexer #(.enable("false")) multiplexer_43 (
    .in0(multiplexer_42_out), .in1(multiplexer_22_out), .sel(undriven));  // open: out
  Multiplexer #(.enable("false")) multiplexer_44 (
    .in1(multiplexer_4_out), .out(multiplexer_44_out), .sel(undriven));  // open: in0
  Multiplexer #(.enable("false")) multiplexer_45 (.in0(multiplexer_44_out), .in1(1'b0), .sel(undriven));  // open: out
  Multiplexer #(.enable("false")) multiplexer_46 (
    .in0(Entrada_A[9]), .in1(Entrada_A[8]), .out(multiplexer_46_out), .sel(undriven));
  Multiplexer #(.enable("false")) multiplexer_47 (
    .in0(multiplexer_46_out), .in1(multiplexer_36_out), .out(multiplexer_47_out), .sel(undriven));
  Multiplexer #(.enable("false")) multiplexer_48 (
    .in0(multiplexer_47_out), .in1(multiplexer_27_out), .out(multiplexer_48_out), .sel(undriven));
  Multiplexer #(.enable("false")) multiplexer_49 (
    .in0(multiplexer_48_out), .in1(multiplexer_8_out), .out(multiplexer_49_out), .sel(undriven));
  Multiplexer #(.enable("false")) multiplexer_50 (.in0(multiplexer_49_out), .in1(1'b0), .sel(undriven));  // open: out
  Multiplexer #(.enable("false")) multiplexer_51 (
    .in0(Entrada_A[10]), .in1(Entrada_A[9]), .out(multiplexer_51_out), .sel(undriven));
  Multiplexer #(.enable("false")) multiplexer_52 (
    .in0(multiplexer_51_out), .in1(multiplexer_41_out), .out(multiplexer_52_out), .sel(undriven));
  Multiplexer #(.enable("false")) multiplexer_53 (
    .in0(multiplexer_52_out), .in1(multiplexer_31_out), .out(multiplexer_53_out), .sel(undriven));
  Multiplexer #(.enable("false")) multiplexer_54 (
    .in0(multiplexer_53_out), .in1(multiplexer_13_out), .out(multiplexer_54_out), .sel(undriven));
  Multiplexer #(.enable("false")) multiplexer_55 (.in0(multiplexer_54_out), .in1(1'b0), .sel(undriven));  // open: out
  Multiplexer #(.enable("false")) multiplexer_56 (
    .in0(Entrada_A[11]), .in1(Entrada_A[10]), .out(multiplexer_56_out), .sel(undriven));
  Multiplexer #(.enable("false")) multiplexer_57 (
    .in0(multiplexer_56_out), .in1(multiplexer_46_out), .out(multiplexer_57_out), .sel(undriven));
  Multiplexer #(.enable("false")) multiplexer_58 (
    .in0(multiplexer_57_out), .in1(multiplexer_37_out), .out(multiplexer_58_out), .sel(undriven));
  Multiplexer #(.enable("false")) multiplexer_59 (
    .in0(Entrada_A[12]), .in1(Entrada_A[11]), .out(multiplexer_59_out), .sel(undriven));
  Multiplexer #(.enable("false")) multiplexer_60 (
    .in0(multiplexer_59_out), .in1(multiplexer_51_out), .out(multiplexer_60_out), .sel(undriven));
  Multiplexer #(.enable("false")) multiplexer_61 (
    .in0(multiplexer_60_out), .in1(multiplexer_42_out), .out(multiplexer_61_out), .sel(undriven));
  Multiplexer #(.enable("false")) multiplexer_62 (
    .in0(multiplexer_58_out), .in1(multiplexer_18_out), .out(multiplexer_62_out), .sel(undriven));
  Multiplexer #(.enable("false")) multiplexer_63 (.in0(multiplexer_62_out), .in1(1'b0), .sel(undriven));  // open: out
  Multiplexer #(.enable("false")) multiplexer_64 (
    .in0(Entrada_A[13]), .in1(Entrada_A[12]), .out(multiplexer_64_out), .sel(undriven));
  Multiplexer #(.enable("false")) multiplexer_65 (
    .in0(multiplexer_64_out), .in1(multiplexer_56_out), .out(multiplexer_65_out), .sel(undriven));
  Multiplexer #(.enable("false")) multiplexer_66 (
    .in0(multiplexer_61_out), .in1(multiplexer_23_out), .out(multiplexer_66_out), .sel(undriven));
  Multiplexer #(.enable("false")) multiplexer_67 (.in0(multiplexer_66_out), .in1(1'b0), .sel(undriven));  // open: out
  Multiplexer #(.enable("false")) multiplexer_68 (
    .in0(multiplexer_65_out), .in1(multiplexer_47_out), .out(multiplexer_68_out), .sel(undriven));
  Multiplexer #(.enable("false")) multiplexer_69 (
    .in0(multiplexer_68_out), .in1(multiplexer_28_out), .out(multiplexer_69_out), .sel(undriven));
  Multiplexer #(.enable("false")) multiplexer_70 (.in0(multiplexer_69_out), .in1(1'b0), .sel(undriven));  // open: out
  Multiplexer #(.enable("false")) multiplexer_71 (
    .in0(Entrada_A[14]), .in1(Entrada_A[13]), .out(multiplexer_71_out), .sel(undriven));
  Multiplexer #(.enable("false")) multiplexer_72 (
    .in0(multiplexer_71_out), .in1(multiplexer_59_out), .out(multiplexer_72_out), .sel(undriven));
  Multiplexer #(.enable("false")) multiplexer_73 (
    .in0(multiplexer_72_out), .in1(multiplexer_52_out), .out(multiplexer_73_out), .sel(undriven));
  Multiplexer #(.enable("false")) multiplexer_74 (
    .in0(multiplexer_73_out), .in1(multiplexer_33_out), .out(multiplexer_74_out), .sel(undriven));
  Multiplexer #(.enable("false")) multiplexer_75 (.in0(multiplexer_74_out), .in1(1'b0), .sel(undriven));  // open: out
  Multiplexer #(.enable("false")) multiplexer_76 (
    .in0(Entrada_A[15]), .in1(Entrada_A[14]), .out(multiplexer_76_out), .sel(undriven));
  Multiplexer #(.enable("false")) multiplexer_77 (
    .in0(multiplexer_76_out), .in1(multiplexer_64_out), .out(multiplexer_77_out), .sel(undriven));
  Multiplexer #(.enable("false")) multiplexer_78 (
    .in0(multiplexer_77_out), .in1(multiplexer_57_out), .out(multiplexer_78_out), .sel(undriven));
  Multiplexer #(.enable("false")) multiplexer_79 (
    .in0(multiplexer_78_out), .in1(multiplexer_38_out), .out(multiplexer_79_out), .sel(undriven));
  Multiplexer #(.enable("false")) multiplexer_80 (.in0(multiplexer_79_out), .in1(1'b0), .sel(undriven));  // open: out
  Multiplexer #(.enable("false")) multiplexer_81 (
    .in0(Entrada_A[16]), .in1(Entrada_A[15]), .out(multiplexer_81_out), .sel(undriven));
  Multiplexer #(.enable("false")) multiplexer_82 (
    .in0(multiplexer_81_out), .in1(multiplexer_71_out), .out(multiplexer_82_out), .sel(undriven));
  Multiplexer #(.enable("false")) multiplexer_83 (
    .in0(multiplexer_82_out), .in1(multiplexer_60_out), .out(multiplexer_83_out), .sel(undriven));
  Multiplexer #(.enable("false")) multiplexer_84 (
    .in0(multiplexer_83_out), .in1(multiplexer_48_out), .out(multiplexer_84_out), .sel(undriven));
  Multiplexer #(.enable("false")) multiplexer_85 (
    .in0(multiplexer_84_out), .in1(multiplexer_5_out), .sel(undriven));  // open: out
  Multiplexer #(.enable("false")) multiplexer_86 (
    .in0(Entrada_A[17]), .in1(Entrada_A[16]), .out(multiplexer_86_out), .sel(undriven));
  Multiplexer #(.enable("false")) multiplexer_87 (
    .in0(multiplexer_86_out), .in1(multiplexer_76_out), .out(multiplexer_87_out), .sel(undriven));
  Multiplexer #(.enable("false")) multiplexer_88 (
    .in0(multiplexer_87_out), .in1(multiplexer_65_out), .out(multiplexer_88_out), .sel(undriven));
  Multiplexer #(.enable("false")) multiplexer_89 (
    .in0(multiplexer_88_out), .in1(multiplexer_53_out), .out(multiplexer_89_out), .sel(undriven));
  Multiplexer #(.enable("false")) multiplexer_90 (
    .in0(multiplexer_89_out), .in1(multiplexer_9_out), .sel(undriven));  // open: out
  Multiplexer #(.enable("false")) multiplexer_91 (
    .in0(Entrada_A[18]), .in1(Entrada_A[17]), .out(multiplexer_91_out), .sel(undriven));
  Multiplexer #(.enable("false")) multiplexer_92 (
    .in0(multiplexer_91_out), .in1(multiplexer_81_out), .out(multiplexer_92_out), .sel(undriven));
  Multiplexer #(.enable("false")) multiplexer_93 (
    .in0(multiplexer_92_out), .in1(multiplexer_72_out), .out(multiplexer_93_out), .sel(undriven));
  Multiplexer #(.enable("false")) multiplexer_94 (
    .in0(Entrada_A[19]), .in1(Entrada_A[18]), .out(multiplexer_94_out), .sel(undriven));
  Multiplexer #(.enable("false")) multiplexer_95 (
    .in0(multiplexer_93_out), .in1(multiplexer_58_out), .out(multiplexer_95_out), .sel(undriven));
  Multiplexer #(.enable("false")) multiplexer_96 (
    .in0(multiplexer_95_out), .in1(multiplexer_14_out), .sel(undriven));  // open: out
  Multiplexer #(.enable("false")) multiplexer_97 (
    .in0(Entrada_A[20]), .in1(Entrada_A[19]), .out(multiplexer_97_out), .sel(undriven));
  Multiplexer #(.enable("false")) multiplexer_98 (
    .in0(multiplexer_94_out), .in1(multiplexer_86_out), .out(multiplexer_98_out), .sel(undriven));
  Multiplexer #(.enable("false")) multiplexer_99 (
    .in0(multiplexer_98_out), .in1(multiplexer_77_out), .out(multiplexer_99_out), .sel(undriven));
  Multiplexer #(.enable("false")) multiplexer_100 (
    .in0(multiplexer_99_out), .in1(multiplexer_61_out), .out(multiplexer_100_out), .sel(undriven));
  Multiplexer #(.enable("false")) multiplexer_101 (
    .in0(multiplexer_100_out), .in1(multiplexer_19_out), .sel(undriven));  // open: out
  Multiplexer #(.enable("false")) multiplexer_102 (
    .in0(multiplexer_97_out), .in1(multiplexer_91_out), .out(multiplexer_102_out), .sel(undriven));
  Multiplexer #(.enable("false")) multiplexer_103 (
    .in0(multiplexer_102_out), .in1(multiplexer_82_out), .out(multiplexer_103_out), .sel(undriven));
  Multiplexer #(.enable("false")) multiplexer_104 (
    .in0(multiplexer_103_out), .in1(multiplexer_68_out), .out(multiplexer_104_out), .sel(undriven));
  Multiplexer #(.enable("false")) multiplexer_105 (
    .in0(multiplexer_104_out), .in1(multiplexer_24_out), .sel(undriven));  // open: out
  Multiplexer #(.enable("false")) multiplexer_106 (
    .in0(Entrada_A[21]), .in1(Entrada_A[20]), .out(multiplexer_106_out), .sel(undriven));
  Multiplexer #(.enable("false")) multiplexer_107 (
    .in0(multiplexer_106_out), .in1(multiplexer_94_out), .out(multiplexer_107_out), .sel(undriven));
  Multiplexer #(.enable("false")) multiplexer_108 (
    .in0(multiplexer_107_out), .in1(multiplexer_87_out), .out(multiplexer_108_out), .sel(undriven));
  Multiplexer #(.enable("false")) multiplexer_109 (
    .in0(multiplexer_108_out), .in1(multiplexer_73_out), .out(multiplexer_109_out), .sel(undriven));
  Multiplexer #(.enable("false")) multiplexer_110 (
    .in0(multiplexer_109_out), .in1(multiplexer_29_out), .sel(undriven));  // open: out
  Multiplexer #(.enable("false")) multiplexer_111 (
    .in0(Entrada_A[22]), .in1(Entrada_A[21]), .out(multiplexer_111_out), .sel(undriven));
  Multiplexer #(.enable("false")) multiplexer_112 (
    .in0(multiplexer_111_out), .in1(multiplexer_97_out), .out(multiplexer_112_out), .sel(undriven));
  Multiplexer #(.enable("false")) multiplexer_113 (
    .in0(multiplexer_112_out), .in1(multiplexer_92_out), .out(multiplexer_113_out), .sel(undriven));
  Multiplexer #(.enable("false")) multiplexer_114 (
    .in0(multiplexer_113_out), .in1(multiplexer_78_out), .out(multiplexer_114_out), .sel(undriven));
  Multiplexer #(.enable("false")) multiplexer_115 (
    .in0(multiplexer_114_out), .in1(multiplexer_34_out), .sel(undriven));  // open: out
  Multiplexer #(.enable("false")) multiplexer_116 (
    .in0(Entrada_A[23]), .in1(Entrada_A[22]), .out(multiplexer_116_out), .sel(undriven));
  Multiplexer #(.enable("false")) multiplexer_117 (
    .in0(multiplexer_116_out), .in1(multiplexer_106_out), .out(multiplexer_117_out), .sel(undriven));
  Multiplexer #(.enable("false")) multiplexer_118 (
    .in0(multiplexer_117_out), .in1(multiplexer_98_out), .out(multiplexer_118_out), .sel(undriven));
  Multiplexer #(.enable("false")) multiplexer_119 (
    .in0(multiplexer_118_out), .in1(multiplexer_83_out), .out(multiplexer_119_out), .sel(undriven));
  Multiplexer #(.enable("false")) multiplexer_120 (
    .in0(Entrada_A[24]), .in1(Entrada_A[23]), .out(multiplexer_120_out), .sel(undriven));
  Multiplexer #(.enable("false")) multiplexer_121 (
    .in0(multiplexer_120_out), .in1(multiplexer_111_out), .out(multiplexer_121_out), .sel(undriven));
  Multiplexer #(.enable("false")) multiplexer_122 (
    .in0(multiplexer_121_out), .in1(multiplexer_102_out), .out(multiplexer_122_out), .sel(undriven));
  Multiplexer #(.enable("false")) multiplexer_123 (
    .in0(multiplexer_122_out), .in1(multiplexer_88_out), .out(multiplexer_123_out), .sel(undriven));
  Multiplexer #(.enable("false")) multiplexer_124 (
    .in0(multiplexer_119_out), .in1(multiplexer_39_out), .sel(undriven));  // open: out
  Multiplexer #(.enable("false")) multiplexer_125 (
    .in0(Entrada_A[25]), .in1(Entrada_A[24]), .out(multiplexer_125_out), .sel(undriven));
  Multiplexer #(.enable("false")) multiplexer_126 (
    .in0(multiplexer_125_out), .in1(multiplexer_116_out), .out(multiplexer_126_out), .sel(undriven));
  Multiplexer #(.enable("false")) multiplexer_127 (
    .in0(multiplexer_126_out), .in1(multiplexer_107_out), .out(multiplexer_127_out), .sel(undriven));
  Multiplexer #(.enable("false")) multiplexer_128 (
    .in0(multiplexer_123_out), .in1(multiplexer_44_out), .sel(undriven));  // open: out
  Multiplexer #(.enable("false")) multiplexer_129 (
    .in0(Entrada_A[26]), .in1(Entrada_A[25]), .out(multiplexer_129_out), .sel(undriven));
  Multiplexer #(.enable("false")) multiplexer_130 (
    .in0(multiplexer_127_out), .in1(multiplexer_93_out), .out(multiplexer_130_out), .sel(undriven));
  Multiplexer #(.enable("false")) multiplexer_131 (
    .in0(multiplexer_130_out), .in1(multiplexer_49_out), .sel(undriven));  // open: out
  Multiplexer #(.enable("false")) multiplexer_132 (
    .in0(multiplexer_129_out), .in1(multiplexer_120_out), .out(multiplexer_132_out), .sel(undriven));
  Multiplexer #(.enable("false")) multiplexer_133 (
    .in0(multiplexer_132_out), .in1(multiplexer_112_out), .out(multiplexer_133_out), .sel(undriven));
  Multiplexer #(.enable("false")) multiplexer_134 (
    .in0(multiplexer_133_out), .in1(multiplexer_99_out), .out(multiplexer_134_out), .sel(undriven));
  Multiplexer #(.enable("false")) multiplexer_135 (
    .in0(multiplexer_134_out), .in1(multiplexer_54_out), .sel(undriven));  // open: out
  Multiplexer #(.enable("false")) multiplexer_136 (
    .in0(Entrada_A[27]), .in1(Entrada_A[26]), .out(multiplexer_136_out), .sel(undriven));
  Multiplexer #(.enable("false")) multiplexer_137 (
    .in0(multiplexer_136_out), .in1(multiplexer_125_out), .out(multiplexer_137_out), .sel(undriven));
  Multiplexer #(.enable("false")) multiplexer_138 (
    .in0(multiplexer_137_out), .in1(multiplexer_117_out), .out(multiplexer_138_out), .sel(undriven));
  Multiplexer #(.enable("false")) multiplexer_139 (
    .in0(multiplexer_138_out), .in1(multiplexer_103_out), .out(multiplexer_139_out), .sel(undriven));
  Multiplexer #(.enable("false")) multiplexer_140 (
    .in0(multiplexer_139_out), .in1(multiplexer_62_out), .sel(undriven));  // open: out
  Multiplexer #(.enable("false")) multiplexer_141 (
    .in0(Entrada_A[28]), .in1(Entrada_A[27]), .out(multiplexer_141_out), .sel(undriven));
  Multiplexer #(.enable("false")) multiplexer_142 (
    .in0(multiplexer_141_out), .in1(multiplexer_129_out), .out(multiplexer_142_out), .sel(undriven));
  Multiplexer #(.enable("false")) multiplexer_143 (
    .in0(multiplexer_142_out), .in1(multiplexer_121_out), .out(multiplexer_143_out), .sel(undriven));
  Multiplexer #(.enable("false")) multiplexer_144 (
    .in0(multiplexer_143_out), .in1(multiplexer_108_out), .out(multiplexer_144_out), .sel(undriven));
  Multiplexer #(.enable("false")) multiplexer_145 (
    .in0(multiplexer_144_out), .in1(multiplexer_66_out), .sel(undriven));  // open: out
  Multiplexer #(.enable("false")) multiplexer_146 (
    .in0(Entrada_A[29]), .in1(Entrada_A[28]), .out(multiplexer_146_out), .sel(undriven));
  Multiplexer #(.enable("false")) multiplexer_147 (
    .in0(multiplexer_146_out), .in1(multiplexer_136_out), .out(multiplexer_147_out), .sel(undriven));
  Multiplexer #(.enable("false")) multiplexer_148 (
    .in0(multiplexer_147_out), .in1(multiplexer_126_out), .out(multiplexer_148_out), .sel(undriven));
  Multiplexer #(.enable("false")) multiplexer_149 (
    .in0(multiplexer_148_out), .in1(multiplexer_113_out), .out(multiplexer_149_out), .sel(undriven));
  Multiplexer #(.enable("false")) multiplexer_150 (
    .in0(multiplexer_149_out), .in1(multiplexer_69_out), .sel(undriven));  // open: out
  Multiplexer #(.enable("false")) multiplexer_151 (
    .in0(Entrada_A[30]), .in1(Entrada_A[29]), .out(multiplexer_151_out), .sel(undriven));
  Multiplexer #(.enable("false")) multiplexer_152 (
    .in0(multiplexer_151_out), .in1(multiplexer_141_out), .out(multiplexer_152_out), .sel(undriven));
  Multiplexer #(.enable("false")) multiplexer_153 (
    .in0(multiplexer_152_out), .in1(multiplexer_132_out), .out(multiplexer_153_out), .sel(undriven));
  Multiplexer #(.enable("false")) multiplexer_154 (
    .in0(multiplexer_153_out), .in1(multiplexer_118_out), .out(multiplexer_154_out), .sel(undriven));
  Multiplexer #(.enable("false")) multiplexer_155 (
    .in0(Entrada_A[31]), .in1(Entrada_A[30]), .out(multiplexer_155_out), .sel(undriven));
  Multiplexer #(.enable("false")) multiplexer_156 (
    .in0(multiplexer_155_out), .in1(multiplexer_146_out), .out(multiplexer_156_out), .sel(undriven));
  Multiplexer #(.enable("false")) multiplexer_157 (
    .in0(multiplexer_154_out), .in1(multiplexer_74_out), .sel(undriven));  // open: out
  Multiplexer #(.enable("false")) multiplexer_158 (
    .in0(multiplexer_156_out), .in1(multiplexer_137_out), .out(multiplexer_158_out), .sel(undriven));
  Multiplexer #(.enable("false")) multiplexer_159 (
    .in0(multiplexer_158_out), .in1(multiplexer_122_out), .out(multiplexer_159_out), .sel(undriven));
  Multiplexer #(.enable("false")) multiplexer_160 (
    .in0(multiplexer_159_out), .in1(multiplexer_79_out), .sel(undriven));  // open: out
endmodule
